# Fritzing sketch hc_sr04-servo_fritzing (saved by Fritzing 0.9.4)
breadboards: 1

parts:
  Part1 = Arduino Uno (Rev3)
  J1 = Basic Servo
  HC-SR04_Sensor_1 = HC-SR04 Ultrasonic Distance Sensor

nets:
  N1: Part1.D10_PWM/SS, HC-SR04_Sensor_1.TRIG
  N2: Part1.D11_PWM/MOSI, HC-SR04_Sensor_1.ECHO
  N3: Part1.D12/MISO, J1.pulse
  VCC: Part1.5V, J1.vcc, HC-SR04_Sensor_1.VCC
  GND: Part1.GND, J1.gnd, HC-SR04_Sensor_1.GND
