# Fritzing sketch servo_cizim (saved by Fritzing 0.9.4)
breadboards: 1

parts:
  Part1 = Arduino Uno (Rev3)
  J1 = Basic Servo
  J2 = Basic Servo
  Part2 = Arduino Uno (Rev3)

nets:
  N1: Part1.D3_PWM, J1.pulse
  5V: Part1.5V, J1.vcc
  GND: Part1.GND, J1.gnd
  GND_2: J2.gnd, Part2.GND
  VCC: J2.vcc, Part2.5V
  N2: J2.pulse, Part2.D3_PWM
